// Logisim project circuito.circ as structural Verilog: 1 circuit, main circuit main
module main (
  input  P,
  input  Q,
  input  P_2,
  input  Q_2,
  input  P_3,
  input  Q_3,
  input  Integrante_1,
  input  Integrante_2,
  input  Integrante_3,
  input  Toby,
  output out_11,
  output out_12,
  output out_13,
  output out_14
);

  wire and_1_out, and_2_out, and_3_out, and_4_out, and_5_out, and_7_out, not_1_out, not_2_out, not_3_out,
       not_4_out, not_5_out, or_2_out, or_3_out, or_4_out, or_5_out;

  not not_1 (not_1_out, P);
  not not_2 (not_2_out, Q);
  not not_3 (not_3_out, P_2);
  not not_4 (not_4_out, P_3);
  not not_5 (not_5_out, Q_3);
  and and_1 (and_1_out, not_1_out, not_2_out);
  not not_6 (out_11, and_1_out);
  or or_1 (out_12, not_3_out, Q_2);
  or or_2 (or_2_out, not_4_out, Q_3);
  or or_3 (or_3_out, not_5_out, P_3);
  and and_2 (and_2_out, Integrante_1, Integrante_2);
  and and_3 (and_3_out, Toby, Integrante_3);
  and and_4 (and_4_out, Toby, Integrante_2);
  and and_5 (and_5_out, Toby, Integrante_1);
  and and_6 (out_13, or_2_out, or_3_out);
  and and_7 (and_7_out, Integrante_3, and_2_out);
  or or_4 (or_4_out, and_7_out, and_3_out);
  or or_5 (or_5_out, and_4_out, and_5_out);
  or or_6 (out_14, or_4_out, or_5_out);

  // Notes on the sheet:
  //   OR usando AND y NEG
  //   Implicacion logica
  //   Equivalencia logica
  //   Problema de Tobi
endmodule
