// Logisim project circuito.circ as structural Verilog: 1 circuit, main circuit main
module main (
  input  W,
  input  X,
  input  Y,
  input  Z,
  input  W_2,
  input  X_2,
  input  Y_2,
  input  Z_2,
  input  T,
  input  X_3,
  input  Y_3,
  input  Z_3,
  input  in_13,
  input  in_14,
  input  in_15,
  input  in_16,
  output out_17,
  output out_18,
  output out_19,
  output out_20,
  output out_21
);

  wire and_1_out, and_2_out, and_3_out, and_4_out, and_5_out, and_6_out, and_7_out, and_8_out, and_9_out,
       and_10_out, and_11_out, and_12_out, nor_1_out, nor_2_out, nor_3_out, not_1_out, not_2_out, not_3_out,
       not_4_out, not_5_out, not_6_out, not_7_out, not_8_out, not_9_out, not_10_out, not_11_out;

  not not_1 (not_1_out, Z);
  not not_2 (not_2_out, Y);
  nor nor_1 (nor_1_out, in_13, in_16);
  and and_1 (and_1_out, W, X, Y, Z);
  and and_2 (and_2_out, W, X, Y, not_1_out);
  not not_3 (not_3_out, Z);
  not not_4 (not_4_out, X);
  not not_5 (not_5_out, Y);
  not not_6 (not_6_out, W);
  not not_7 (not_7_out, X);
  not not_8 (not_8_out, Y);
  not not_9 (not_9_out, X_2);
  not not_10 (not_10_out, Y_2);
  nor nor_2 (nor_2_out, in_13, nor_1_out);
  nor nor_3 (nor_3_out, nor_1_out, in_16);
  and and_3 (and_3_out, W, X, not_2_out, not_3_out);
  and and_4 (and_4_out, W, not_4_out, not_5_out, Z);
  and and_5 (and_5_out, not_6_out, not_7_out, not_8_out, Z);
  not not_11 (not_11_out, Y);
  and and_6 (and_6_out, W_2, X_2);
  and and_7 (and_7_out, not_9_out, not_10_out, Z_2);
  and and_8 (and_8_out, T, X_3);
  and and_9 (and_9_out, X_3, Y_3, Z_3);
  and and_10 (and_10_out, T, Z_3);
  and and_11 (and_11_out, T, Y_3);
  nor nor_4 (out_21, nor_2_out, nor_3_out);
  and and_12 (and_12_out, W, X, not_11_out, Z);
  or or_1 (out_18, and_6_out, and_7_out);
  or or_2 (out_17, and_1_out, and_2_out, and_3_out, and_4_out, and_5_out, and_12_out);
  or or_3 (out_19, and_8_out, and_9_out, and_10_out, and_11_out);
  xor xor_1 (out_20, in_14, in_15);

  // Notes on the sheet:
  //   Original
  //   Reducido
  //   Motin
  //   Equivalencia
  //   Esto es 
  //   equivalente a:
endmodule
