// Logisim project circuito.circ as structural Verilog: 1 circuit, main circuit main
module main (
  input  A,
  input  B,
  input  C,
  input  D,
  input  A_2,
  input  B_2,
  input  C_2,
  input  A_3,
  input  B_3,
  input  C_3,
  input  A_4,
  input  B_4,
  input  C_4,
  output out_14,
  output out_15,
  output out_16,
  output out_17
);

  wire and_1_out, and_2_out, and_3_out, and_4_out, and_5_out, and_6_out, and_7_out, and_8_out, and_9_out,
       not_1_out, not_2_out, not_3_out, not_4_out, not_5_out, not_6_out, not_7_out;

  not not_1 (not_1_out, D);
  not not_2 (not_2_out, C);
  not not_3 (not_3_out, D);
  not not_4 (not_4_out, C);
  not not_5 (not_5_out, D);
  not not_6 (not_6_out, B_3);
  not not_7 (not_7_out, C_3);
  and and_1 (and_1_out, A, not_1_out, not_2_out);
  and and_2 (and_2_out, B, not_3_out, not_4_out);
  and and_3 (and_3_out, C, not_5_out);
  and and_4 (and_4_out, A_2, B_2);
  and and_5 (and_5_out, A_3, not_6_out);
  and and_6 (and_6_out, B_3, not_7_out);
  and and_7 (and_7_out, A_4, C_4);
  and and_8 (and_8_out, A_4, B_4);
  and and_9 (and_9_out, B_4, C_4);
  or or_1 (out_15, and_4_out, C_2);
  or or_2 (out_16, and_5_out, and_6_out);
  or or_3 (out_14, and_1_out, and_2_out, and_3_out);
  or or_4 (out_17, and_7_out, and_8_out, and_9_out);

  // Notes on the sheet:
  //   Expresion reducida 1
  //   Expresion reducida 2
  //   Expresion reducida 3
  //   Expresion reducida 4
endmodule
