// Logisim project circuito.circ as structural Verilog: 1 circuit, main circuit main
module main (
  input  in_1,
  input  in_2,
  input  in_3,
  input  in_4,
  input  Toby_siempre_activo,
  input  Toby,
  input  Bff,
  input  in_8,
  input  in_9,
  input  in_10,
  input  in_11,
  input  in_12,
  input  in_13,
  input  in_14,
  input  in_15,
  input  in_16,
  input  in_17,
  input  in_18,
  input  in_19,
  input  in_20,
  input  in_21,
  input  in_22,
  input  in_23,
  input  in_24,
  input  in_25,
  input  in_26,
  input  in_27,
  input  in_28,
  input  in_29,
  input  in_30,
  input  in_31,
  input  in_32,
  input  in_33,
  input  in_34,
  input  in_35,
  input  in_36,
  input  in_37,
  input  in_38,
  input  in_39,
  input  in_40,
  input  in_41,
  input  in_42,
  input  in_43,
  input  in_44,
  input  in_45,
  input  in_46,
  input  in_47,
  input  in_48,
  input  in_49,
  input  in_50,
  input  in_51,
  input  in_52,
  output out_53,
  output out_54,
  output out_55,
  output out_56,
  output out_57,
  output out_58,
  output out_59,
  output out_60,
  output out_61,
  output out_62,
  output out_63,
  output out_64,
  output out_65,
  output out_66,
  output out_67,
  output out_68,
  output out_69,
  output out_70,
  output out_71,
  output out_72,
  output out_73,
  output out_74,
  output out_75,
  output out_76,
  output out_77,
  output out_78,
  output out_79,
  output out_80,
  output out_81,
  output out_82,
  output out_83,
  output out_84,
  output out_85,
  output out_86,
  output out_87,
  output out_88,
  output out_89,
  output out_90,
  output out_91,
  output out_92,
  output out_93,
  output out_94,
  output out_95,
  output out_96,
  output out_97,
  output out_98,
  output out_99,
  output out_100,
  output out_101,
  output out_102,
  output out_103,
  output out_104,
  output out_105,
  output out_106,
  output out_107,
  output out_108,
  output out_109,
  output out_110,
  output out_111,
  output out_112,
  output out_113,
  output out_114,
  output out_115,
  output out_116,
  output out_117,
  output out_118,
  output out_119,
  output out_120,
  output out_121,
  output out_122,
  output out_123,
  output out_124,
  output out_125,
  output out_126,
  output out_127,
  output out_128,
  output out_129,
  output out_130,
  output out_131,
  output out_132,
  output out_133,
  output out_134
);

  wire and_5_out, and_6_out, and_7_out, and_8_out, and_17_out, and_18_out, and_19_out, and_20_out,
       and_41_out, not_1_out, not_2_out, not_3_out, not_4_out, not_5_out, not_6_out, not_7_out, not_8_out,
       not_9_out, not_10_out, not_11_out, not_12_out, not_13_out, not_14_out, not_15_out, not_16_out,
       not_17_out, not_18_out, not_19_out, not_20_out, not_21_out, not_22_out, not_23_out, not_24_out,
       not_25_out, not_26_out, not_27_out, not_28_out, not_29_out, not_30_out, not_31_out, not_32_out,
       not_33_out, not_34_out, not_35_out, not_36_out, not_37_out, not_38_out, not_39_out, not_40_out,
       not_41_out, not_42_out, not_43_out, not_44_out, not_45_out, not_46_out, or_3_out, or_4_out, or_5_out,
       or_6_out, or_10_out, or_11_out, or_12_out, or_13_out, or_14_out, or_15_out, or_16_out, or_17_out,
       or_18_out, or_19_out, or_20_out, or_21_out, or_22_out, or_23_out, or_24_out;

  not not_1 (not_1_out, in_1);
  not not_2 (not_2_out, in_3);
  not not_3 (not_3_out, in_13);
  and and_1 (out_53, not_1_out, not_2_out);
  and and_2 (out_55, in_1, not_2_out);
  and and_3 (out_58, not_1_out, in_3);
  and and_4 (out_60, in_1, in_3);
  not not_4 (not_4_out, in_23);
  not not_5 (not_5_out, in_24);
  or or_1 (out_126, in_25, in_28);
  or or_2 (out_129, in_25, in_31);
  not not_6 (not_6_out, in_9);
  not not_7 (not_7_out, in_11);
  not not_8 (not_8_out, in_9);
  not not_9 (not_9_out, in_11);
  not not_10 (not_10_out, in_18);
  not not_11 (not_11_out, in_19);
  and and_5 (and_5_out, not_4_out, not_5_out);
  and and_6 (and_6_out, in_23, not_5_out);
  and and_7 (and_7_out, not_4_out, in_24);
  and and_8 (and_8_out, in_23, in_24);
  and and_9 (out_62, not_6_out, not_3_out, not_7_out);
  and and_10 (out_64, in_9, not_3_out, not_7_out);
  and and_11 (out_66, not_6_out, not_3_out, in_11);
  and and_12 (out_68, in_9, not_3_out, in_11);
  and and_13 (out_70, not_8_out, in_13, not_9_out);
  and and_14 (out_72, in_9, in_13, not_9_out);
  and and_15 (out_74, not_8_out, in_13, in_11);
  and and_16 (out_76, in_9, in_13, in_11);
  and and_17 (and_17_out, not_10_out, not_11_out);
  and and_18 (and_18_out, in_18, not_11_out);
  and and_19 (and_19_out, not_10_out, in_19);
  and and_20 (and_20_out, in_18, in_19);
  or or_3 (or_3_out, in_26, in_29);
  or or_4 (or_4_out, in_26, in_32);
  or or_5 (or_5_out, in_37, in_39);
  or or_6 (or_6_out, in_37, in_41);
  not not_12 (not_12_out, in_2);
  not not_13 (not_13_out, in_4);
  and and_21 (out_54, not_12_out, in_8, not_13_out);
  and and_22 (out_56, in_2, in_8, not_13_out);
  and and_23 (out_59, not_12_out, in_8, in_4);
  and and_24 (out_61, in_2, in_8, in_4);
  or or_7 (out_127, or_3_out, or_5_out);
  or or_8 (out_130, or_4_out, or_6_out);
  or or_9 (out_132, in_35, in_43);
  not not_14 (not_14_out, in_16);
  not not_15 (not_15_out, in_17);
  not not_16 (not_16_out, in_16);
  not not_17 (not_17_out, in_17);
  not not_18 (not_18_out, in_16);
  not not_19 (not_19_out, in_17);
  not not_20 (not_20_out, in_16);
  not not_21 (not_21_out, in_17);
  not not_22 (not_22_out, in_14);
  and and_25 (out_78, not_14_out, and_17_out, not_15_out);
  and and_26 (out_79, in_16, and_17_out, not_15_out);
  and and_27 (out_80, not_14_out, and_17_out, in_17);
  and and_28 (out_81, in_16, and_17_out, in_17);
  and and_29 (out_82, not_16_out, and_18_out, not_17_out);
  and and_30 (out_83, in_16, and_18_out, not_17_out);
  and and_31 (out_84, not_16_out, and_18_out, in_17);
  and and_32 (out_85, in_16, and_18_out, in_17);
  and and_33 (out_86, not_18_out, and_19_out, not_19_out);
  and and_34 (out_87, in_16, and_19_out, not_19_out);
  and and_35 (out_88, not_18_out, and_19_out, in_17);
  and and_36 (out_89, in_16, and_19_out, in_17);
  and and_37 (out_90, not_20_out, and_20_out, not_21_out);
  and and_38 (out_91, in_16, and_20_out, not_21_out);
  and and_39 (out_92, not_20_out, and_20_out, in_17);
  and and_40 (out_93, in_16, and_20_out, in_17);
  and and_41 (and_41_out, Toby_siempre_activo, Toby);
  or or_10 (or_10_out, in_27, in_30);
  or or_11 (or_11_out, in_27, in_33);
  or or_12 (or_12_out, in_38, in_40);
  or or_13 (or_13_out, in_38, in_42);
  or or_14 (or_14_out, in_45, in_46);
  or or_15 (or_15_out, in_45, in_47);
  or or_16 (or_16_out, in_49, in_50);
  or or_17 (or_17_out, in_49, in_51);
  not not_23 (not_23_out, in_10);
  not not_24 (not_24_out, in_12);
  not not_25 (not_25_out, in_10);
  not not_26 (not_26_out, in_12);
  not not_27 (not_27_out, in_22);
  not not_28 (not_28_out, in_22);
  not not_29 (not_29_out, in_22);
  not not_30 (not_30_out, in_22);
  or or_18 (or_18_out, or_10_out, or_12_out);
  or or_19 (or_19_out, or_11_out, or_13_out);
  or or_20 (or_20_out, in_36, in_44);
  or or_21 (or_21_out, or_14_out, or_16_out);
  or or_22 (or_22_out, or_15_out, or_17_out);
  or or_23 (or_23_out, in_48, in_52);
  and and_42 (out_57, and_41_out, Bff);
  and and_43 (out_63, not_23_out, not_22_out, in_15, not_24_out);
  and and_44 (out_65, in_10, not_22_out, in_15, not_24_out);
  and and_45 (out_67, not_23_out, not_22_out, in_15, in_12);
  and and_46 (out_69, in_10, not_22_out, in_15, in_12);
  and and_47 (out_71, not_25_out, in_14, in_15, not_26_out);
  and and_48 (out_73, in_10, in_14, in_15, not_26_out);
  and and_49 (out_75, not_25_out, in_14, in_15, in_12);
  and and_50 (out_77, in_10, in_14, in_15, in_12);
  not not_31 (not_31_out, in_20);
  not not_32 (not_32_out, in_21);
  not not_33 (not_33_out, in_20);
  not not_34 (not_34_out, in_21);
  not not_35 (not_35_out, in_20);
  not not_36 (not_36_out, in_21);
  not not_37 (not_37_out, in_20);
  not not_38 (not_38_out, in_21);
  not not_39 (not_39_out, in_20);
  not not_40 (not_40_out, in_21);
  not not_41 (not_41_out, in_20);
  not not_42 (not_42_out, in_21);
  not not_43 (not_43_out, in_20);
  not not_44 (not_44_out, in_21);
  not not_45 (not_45_out, in_20);
  not not_46 (not_46_out, in_21);
  or or_24 (or_24_out, or_20_out, or_23_out);
  and and_51 (out_94, not_31_out, not_27_out, and_5_out, not_32_out);
  and and_52 (out_95, in_20, not_27_out, and_5_out, not_32_out);
  and and_53 (out_96, not_31_out, not_27_out, and_5_out, in_21);
  and and_54 (out_97, in_20, not_27_out, and_5_out, in_21);
  and and_55 (out_98, not_33_out, in_22, and_5_out, not_34_out);
  and and_56 (out_99, in_20, in_22, and_5_out, not_34_out);
  and and_57 (out_100, not_33_out, in_22, and_5_out, in_21);
  and and_58 (out_101, in_20, in_22, and_5_out, in_21);
  and and_59 (out_102, not_35_out, not_28_out, and_6_out, not_36_out);
  and and_60 (out_103, in_20, not_28_out, and_6_out, not_36_out);
  and and_61 (out_104, not_35_out, not_28_out, and_6_out, in_21);
  and and_62 (out_105, in_20, not_28_out, and_6_out, in_21);
  and and_63 (out_106, not_37_out, in_22, and_6_out, not_38_out);
  and and_64 (out_107, in_20, in_22, and_6_out, not_38_out);
  and and_65 (out_108, not_37_out, in_22, and_6_out, in_21);
  and and_66 (out_109, in_20, in_22, and_6_out, in_21);
  and and_67 (out_110, not_39_out, not_29_out, and_7_out, not_40_out);
  and and_68 (out_111, in_20, not_29_out, and_7_out, not_40_out);
  and and_69 (out_112, not_39_out, not_29_out, and_7_out, in_21);
  and and_70 (out_113, in_20, not_29_out, and_7_out, in_21);
  and and_71 (out_114, not_41_out, in_22, and_7_out, not_42_out);
  and and_72 (out_115, in_20, in_22, and_7_out, not_42_out);
  and and_73 (out_116, not_41_out, in_22, and_7_out, in_21);
  and and_74 (out_117, in_20, in_22, and_7_out, in_21);
  and and_75 (out_118, not_43_out, not_30_out, and_8_out, not_44_out);
  and and_76 (out_119, in_20, not_30_out, and_8_out, not_44_out);
  and and_77 (out_120, not_43_out, not_30_out, and_8_out, in_21);
  and and_78 (out_121, in_20, not_30_out, and_8_out, in_21);
  and and_79 (out_122, not_45_out, in_22, and_8_out, not_46_out);
  and and_80 (out_123, in_20, in_22, and_8_out, not_46_out);
  and and_81 (out_124, not_45_out, in_22, and_8_out, in_21);
  and and_82 (out_125, in_20, in_22, and_8_out, in_21);
  or or_25 (out_128, or_18_out, or_21_out);
  or or_26 (out_131, or_18_out, or_22_out);
  or or_27 (out_133, or_22_out, or_19_out);
  or or_28 (out_134, or_22_out, or_21_out);

  // Notes on the sheet:
  //   Decodificador 2x4
  //   Codificador 4x2
  //   Decodificador 3x8 a partir de 2x4
  //   Problema de tobi
  //   Decodificador 2x4 con enable
  //   Codificador 8x3
  //   Decodificador 4x16 a partir de 2x4
  //   Decodificador 5x32 a partir de 3x8
  //   Decodificador 3x8 a partir de 2x4 con enable
  //   Problema de toby con compuertas logicas
  //   Codificador 16x4
endmodule
