// Logisim project circuito.circ as structural Verilog: 2 circuits, main circuit main
module main (
);

  wire and_1_out, and_2_out, and_3_out, and_4_out, and_5_out, and_6_out, bcd_1_out_5, bcd_1_out_6,
       bcd_1_out_7, bcd_1_out_8, bcd_1_out_9, bcd_1_out_10, bcd_1_out_11, bcd_2_out_5, bcd_2_out_6,
       bcd_2_out_7, bcd_2_out_8, bcd_2_out_9, bcd_2_out_10, bcd_2_out_11, bcd_3_out_5, bcd_3_out_6,
       bcd_3_out_7, bcd_3_out_8, bcd_3_out_9, bcd_3_out_10, bcd_3_out_11, bcd_4_out_5, bcd_4_out_6,
       bcd_4_out_7, bcd_4_out_8, bcd_4_out_9, bcd_4_out_10, bcd_4_out_11, clock_1_out, clock_2_out,
       j_k_ff_1_q, j_k_ff_1_qn, j_k_ff_2_q, j_k_ff_2_qn, j_k_ff_3_q, j_k_ff_3_qn, j_k_ff_4_q, j_k_ff_4_qn,
       j_k_ff_5_q, j_k_ff_5_qn, j_k_ff_6_q, j_k_ff_6_qn, j_k_ff_7_q, j_k_ff_7_qn, j_k_ff_8_q, j_k_ff_8_qn,
       j_k_ff_9_q, j_k_ff_9_qn, j_k_ff_10_q, j_k_ff_10_qn, j_k_ff_11_q, j_k_ff_11_qn, j_k_ff_12_q,
       j_k_ff_13_q, j_k_ff_13_qn, j_k_ff_14_q, j_k_ff_14_qn, j_k_ff_15_q, j_k_ff_16_q, j_k_ff_16_qn,
       j_k_ff_17_qn, j_k_ff_18_qn, or_1_out, or_2_out;

  Clock clock_1 (.out(clock_1_out));
  Clock clock_2 (.out(clock_2_out));
  J_K_Flip_Flop j_k_ff_1 (
    .J(1'b1), .clk(clock_1_out), .K(1'b1), .Q(j_k_ff_1_q), .Qn(j_k_ff_1_qn), .en(1'b1), .reset(and_3_out));  // open: preset
  or or_1 (or_1_out, and_6_out, and_1_out);
  and and_1 (and_1_out, j_k_ff_18_qn, j_k_ff_7_q, j_k_ff_2_q);
  or or_2 (or_2_out, and_4_out, and_2_out);
  J_K_Flip_Flop j_k_ff_2 (
    .J(1'b1), .clk(or_1_out), .K(1'b1), .Q(j_k_ff_2_q), .Qn(j_k_ff_2_qn), .reset(or_2_out));  // open: preset, en
  and and_2 (and_2_out, j_k_ff_17_qn, j_k_ff_2_q, j_k_ff_3_q);
  J_K_Flip_Flop j_k_ff_3 (
    .J(1'b1), .clk(or_2_out), .K(1'b1), .Q(j_k_ff_3_q), .Qn(j_k_ff_3_qn), .reset(and_5_out));  // open: preset, en
  and and_3 (and_3_out, j_k_ff_12_q, j_k_ff_6_q);
  bcd bcd_1 (
    .in_1(j_k_ff_12_q), .in_2(j_k_ff_8_q), .in_3(j_k_ff_6_q), .in_4(j_k_ff_1_q), .out_5(bcd_1_out_5),
    .out_6(bcd_1_out_6), .out_7(bcd_1_out_7), .out_8(bcd_1_out_8), .out_9(bcd_1_out_9),
    .out_10(bcd_1_out_10), .out_11(bcd_1_out_11));
  and and_4 (and_4_out, j_k_ff_14_q, j_k_ff_4_q);
  J_K_Flip_Flop j_k_ff_4 (
    .J(1'b1), .clk(j_k_ff_2_qn), .K(1'b1), .Q(j_k_ff_4_q), .Qn(j_k_ff_4_qn), .reset(or_2_out));  // open: preset, en
  and and_5 (and_5_out, j_k_ff_15_q, j_k_ff_5_q);
  J_K_Flip_Flop j_k_ff_5 (
    .J(1'b1), .clk(j_k_ff_3_qn), .K(1'b1), .Q(j_k_ff_5_q), .Qn(j_k_ff_5_qn), .reset(and_5_out));  // open: preset, en
  J_K_Flip_Flop j_k_ff_6 (
    .J(1'b1), .clk(j_k_ff_1_qn), .K(1'b1), .Q(j_k_ff_6_q), .Qn(j_k_ff_6_qn), .en(1'b1), .reset(and_3_out));  // open: preset
  _7_Segment_Display u_7_segment_display_1 (
    .g(bcd_1_out_11), .f(bcd_1_out_10), .a(bcd_1_out_5), .b(bcd_1_out_6), .e(bcd_1_out_9), .d(bcd_1_out_8),
    .c(bcd_1_out_7));  // open: dp
  and and_6 (and_6_out, j_k_ff_16_q, j_k_ff_9_q);
  J_K_Flip_Flop j_k_ff_7 (
    .J(1'b1), .clk(clock_2_out), .K(1'b1), .Q(j_k_ff_7_q), .Qn(j_k_ff_7_qn), .en(1'b1), .reset(or_1_out));  // open: preset
  bcd bcd_2 (
    .in_1(j_k_ff_16_q), .in_2(j_k_ff_13_q), .in_3(j_k_ff_9_q), .in_4(j_k_ff_7_q), .out_5(bcd_2_out_5),
    .out_6(bcd_2_out_6), .out_7(bcd_2_out_7), .out_8(bcd_2_out_8), .out_9(bcd_2_out_9),
    .out_10(bcd_2_out_10), .out_11(bcd_2_out_11));
  J_K_Flip_Flop j_k_ff_8 (
    .J(1'b1), .clk(j_k_ff_6_qn), .K(1'b1), .Q(j_k_ff_8_q), .Qn(j_k_ff_8_qn), .en(1'b1), .reset(and_3_out));  // open: preset
  J_K_Flip_Flop j_k_ff_9 (
    .J(1'b1), .clk(j_k_ff_7_qn), .K(1'b1), .Q(j_k_ff_9_q), .Qn(j_k_ff_9_qn), .en(1'b1), .reset(or_1_out));  // open: preset
  _7_Segment_Display u_7_segment_display_2 (
    .g(bcd_2_out_11), .f(bcd_2_out_10), .a(bcd_2_out_5), .b(bcd_2_out_6), .e(bcd_2_out_9), .d(bcd_2_out_8),
    .c(bcd_2_out_7));  // open: dp
  J_K_Flip_Flop j_k_ff_10 (
    .J(1'b1), .clk(j_k_ff_4_qn), .K(1'b1), .Q(j_k_ff_10_q), .Qn(j_k_ff_10_qn), .reset(or_2_out));  // open: preset, en
  J_K_Flip_Flop j_k_ff_11 (
    .J(1'b1), .clk(j_k_ff_5_qn), .K(1'b1), .Q(j_k_ff_11_q), .Qn(j_k_ff_11_qn), .reset(and_5_out));  // open: preset, en
  J_K_Flip_Flop j_k_ff_12 (
    .J(1'b1), .clk(j_k_ff_8_qn), .K(1'b1), .Q(j_k_ff_12_q), .en(1'b1), .reset(and_3_out));  // open: Qn, preset
  J_K_Flip_Flop j_k_ff_13 (
    .J(1'b1), .clk(j_k_ff_9_qn), .K(1'b1), .Q(j_k_ff_13_q), .Qn(j_k_ff_13_qn), .en(1'b1), .reset(or_1_out));  // open: preset
  J_K_Flip_Flop j_k_ff_14 (
    .J(1'b1), .clk(j_k_ff_10_qn), .K(1'b1), .Q(j_k_ff_14_q), .Qn(j_k_ff_14_qn), .reset(or_2_out));  // open: preset, en
  J_K_Flip_Flop j_k_ff_15 (
    .J(1'b1), .clk(j_k_ff_11_qn), .K(1'b1), .Q(j_k_ff_15_q), .reset(and_5_out));  // open: Qn, preset, en
  J_K_Flip_Flop j_k_ff_16 (
    .J(1'b1), .clk(j_k_ff_13_qn), .K(1'b1), .Q(j_k_ff_16_q), .Qn(j_k_ff_16_qn), .en(1'b1), .reset(or_1_out));  // open: preset
  J_K_Flip_Flop j_k_ff_17 (
    .J(1'b1), .clk(j_k_ff_14_qn), .K(1'b1), .Qn(j_k_ff_17_qn), .en(1'b1));  // open: Q, preset, reset
  bcd bcd_3 (
    .in_1(j_k_ff_14_q), .in_2(j_k_ff_10_q), .in_3(j_k_ff_4_q), .in_4(j_k_ff_2_q), .out_5(bcd_3_out_5),
    .out_6(bcd_3_out_6), .out_7(bcd_3_out_7), .out_8(bcd_3_out_8), .out_9(bcd_3_out_9),
    .out_10(bcd_3_out_10), .out_11(bcd_3_out_11));
  bcd bcd_4 (
    .in_1(j_k_ff_15_q), .in_2(j_k_ff_11_q), .in_3(j_k_ff_5_q), .in_4(j_k_ff_3_q), .out_5(bcd_4_out_5),
    .out_6(bcd_4_out_6), .out_7(bcd_4_out_7), .out_8(bcd_4_out_8), .out_9(bcd_4_out_9),
    .out_10(bcd_4_out_10), .out_11(bcd_4_out_11));
  J_K_Flip_Flop j_k_ff_18 (
    .J(1'b1), .clk(j_k_ff_16_qn), .K(1'b1), .Qn(j_k_ff_18_qn), .en(1'b1));  // open: Q, preset, reset
  _7_Segment_Display u_7_segment_display_3 (
    .g(bcd_3_out_11), .f(bcd_3_out_10), .a(bcd_3_out_5), .b(bcd_3_out_6), .e(bcd_3_out_9), .d(bcd_3_out_8),
    .c(bcd_3_out_7));  // open: dp
  _7_Segment_Display u_7_segment_display_4 (
    .g(bcd_4_out_11), .f(bcd_4_out_10), .a(bcd_4_out_5), .b(bcd_4_out_6), .e(bcd_4_out_9), .d(bcd_4_out_8),
    .c(bcd_4_out_7));  // open: dp

  // Notes on the sheet:
  //   Contdor de 0 a 9
  //   Contador de 0 a 999
  //   Unidad
  //   Decena
endmodule

module bcd (
  input  in_1,
  input  in_2,
  input  in_3,
  input  in_4,
  output out_5,
  output out_6,
  output out_7,
  output out_8,
  output out_9,
  output out_10,
  output out_11
);

  wire and_1_out, and_2_out, and_3_out, and_4_out, and_5_out, and_6_out, and_7_out, and_8_out, and_9_out,
       and_10_out, and_11_out, and_12_out, and_13_out, and_14_out, and_15_out, and_16_out, not_1_out,
       not_2_out, not_3_out, not_4_out, not_5_out, not_6_out, not_7_out, not_8_out, not_9_out, not_10_out,
       not_11_out, not_12_out, not_13_out, not_14_out, not_15_out, not_16_out, not_17_out, not_18_out,
       not_19_out, not_20_out, not_21_out;

  not not_1 (not_1_out, in_2);
  not not_2 (not_2_out, in_4);
  not not_3 (not_3_out, in_3);
  not not_4 (not_4_out, in_4);
  not not_5 (not_5_out, in_3);
  not not_6 (not_6_out, in_2);
  not not_7 (not_7_out, in_4);
  not not_8 (not_8_out, in_2);
  not not_9 (not_9_out, in_4);
  not not_10 (not_10_out, in_3);
  not not_11 (not_11_out, in_2);
  not not_12 (not_12_out, in_4);
  not not_13 (not_13_out, in_4);
  not not_14 (not_14_out, in_3);
  not not_15 (not_15_out, in_4);
  not not_16 (not_16_out, in_3);
  not not_17 (not_17_out, in_4);
  not not_18 (not_18_out, in_2);
  not not_19 (not_19_out, in_4);
  not not_20 (not_20_out, in_3);
  and and_1 (and_1_out, not_1_out, not_2_out);
  and and_2 (and_2_out, in_2, in_4);
  not not_21 (not_21_out, in_2);
  and and_3 (and_3_out, not_3_out, not_4_out);
  and and_4 (and_4_out, in_3, in_4);
  or or_1 (out_7, not_5_out, in_4, in_2);
  and and_5 (and_5_out, not_6_out, not_7_out);
  and and_6 (and_6_out, not_8_out, in_3);
  and and_7 (and_7_out, in_3, not_9_out);
  and and_8 (and_8_out, in_2, not_10_out, in_4);
  and and_9 (and_9_out, not_11_out, not_12_out);
  and and_10 (and_10_out, in_3, not_13_out);
  and and_11 (and_11_out, not_14_out, not_15_out);
  and and_12 (and_12_out, in_2, not_16_out);
  and and_13 (and_13_out, in_2, not_17_out);
  and and_14 (and_14_out, not_18_out, in_3);
  and and_15 (and_15_out, in_3, not_19_out);
  and and_16 (and_16_out, in_2, not_20_out);
  or or_2 (out_5, and_1_out, in_3, and_2_out, in_1);
  or or_3 (out_6, not_21_out, and_3_out, and_4_out);
  or or_4 (out_8, and_5_out, and_6_out, and_7_out, and_8_out);
  or or_5 (out_9, and_9_out, and_10_out);
  or or_6 (out_10, and_11_out, and_12_out, and_13_out, in_1);
  or or_7 (out_11, and_14_out, and_15_out, and_16_out, in_1);
endmodule
